# Fritzing sketch Solenoid_Control (saved by Fritzing 0.9.2b)
breadboards: 1

parts:
  Q1 = Basic FET N-Channel [package="D2Pak [SMD]"]
  R1 = Resistor [tolerance=±20% resistance=100 package=THT]
  D1 = Rectifier Diode [part_number=1N4001 package="300 mil [THT]"]
  L1 = Solenoid
  R2 = Resistor [tolerance=±5% resistance=10k package=THT]

nets:
  N1: Q1.Gate, R1.Pin_1, R2.Pin_0
  N2: Q1.drain, D1.anode, L1.pin1
  GND: Q1.source, R2.Pin_1
  3.3V from MCU: R1.Pin_0
  12V: D1.cathode, L1.pin2

notes:
  Solenoid
  Mosfet-N
