# Fritzing sketch dispenser_stepper_control (saved by Fritzing 0.9.2b)
perfboards: 1

parts:
  U1 = 555 Timer [package="DIP8 [THT]"]
  M1 = Stepper Motor - Bipolar
  R1 = Resistor [tolerance=±5% resistance=4.7k package=THT]
  Power_plug1 = Power plug
  C2 = Ceramic Capacitor [capacitance=0.1nF package="100 mil [THT, multilayer]"]
  C3 = Ceramic Capacitor [capacitance=2.2nF package="100 mil [THT, multilayer]"]
  R2 = Resistor [tolerance=±5% resistance=1M package=THT]
  R3 = Resistor [tolerance=±5% resistance=4.7k package=THT]
  SPEED = Rotary Potentiometer (Small) [maximum_resistance=1MΩ package=THT]
  ENABLE = Toggle Switch [package=THT]
  C1 = Electrolytic Capacitor [capacitance=100µF voltage=16V package="100 mil [THT, electrolytic]"]
  DRV1 = DRV8824

nets:
  GND: U1.Ground, Power_plug1.GND, C2.0, C3.1, ENABLE.COM, C1.-, DRV1.7_-_DIR, DRV1.8_-_GND_logic, DRV1.14_-_GND_motor
  N1: U1.Trigger, U1.Threshold, C3.0, SPEED.leg1, SPEED.wiper
  N2: U1.Output, DRV1.6_-_STEP
  5V: U1.Reset, U1.Vcc_Supply_Voltage, R1.Pin_1, Power_plug1.VCC, R2.Pin_1, C1.+, DRV1.9_-_/FAULT, DRV1.15_-_VMOT
  N3: U1.Control_Voltage, C2.1
  N4: U1.Discharge, R2.Pin_0, R3.Pin_1
  N5: M1.A, DRV1.13_-_B2
  N6: M1.C, DRV1.12_-_B1
  N7: M1.B, DRV1.11_-_A1
  N8: M1.D, DRV1.10_-_A2
  N9: R1.Pin_0, ENABLE.L1, DRV1.0_-_/EN
  N10: R3.Pin_0, SPEED.leg2

custom parts:
  DRV8824: Pololu DRV8824 Stepper Motor Control Breakout The DRV8824 stepper motor driver carrier is a breakout board for TI’s DRV8824 microstepping bipolar stepper motor driver, a lower-current version of the DRV8825. The DRV8824 carrier can only deliver up to 0.75 A per coil without a heat sink (it is rated for up to 1.2 A per coil with sufficient additional cooling), but it has larger current-sense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
